# Fritzing sketch breathalyzerSchematic (saved by Fritzing 0.7.5b)
breadboards: 1

parts:
  Arduino1 = Arduino
  LED1 = RGB LED (com. anode, rbg) [package="5 mm [THT]"]
  Part1 = Gas Sensor Breakout Board
  R1 = Resistor [tolerance=±5% resistance=10k package=THT]

nets:
  N1: Arduino1.D11, LED1.green_cathode
  N2: Arduino1.D10, LED1.common_anode
  N3: Arduino1.D9, LED1.red_cathode
  N4: Arduino1.D3, Part1.B2
  N5: Arduino1.+5V, Part1.A1, Part1.A2, Part1.H1
  GND: Arduino1.GND, LED1.blue_cathode, Part1.GND, R1.Pin_1
  N6: Part1.B1, R1.Pin_0
